# Fritzing sketch wiring esp32 (saved by Fritzing 0.9.5d)
breadboards: 1

parts:
  HC-SR04_Sensor_2 = HC-SR04 Ultrasonic Distance Sensor
  JACK1 = 2.1mm Barrel Jack with Terminal Block
  HC-SR04_Sensor_3 = HC-SR04 Ultrasonic Distance Sensor
  U1 = ESP32S-HiLetgo [part_number=ESP32S-HiLetgo]
  J1 = Basic Servo
  LCD2004-I2C1 = LCD2004-I2C
  LED1 = LED - 3mm [color="Red (633nm)" package="3 mm [THT]"]
  LED2 = LED - 3mm [color="Green (555nm)" package="3 mm [THT]"]
  R1 = Resistor [tolerance=±5% resistance=220 package="0402 [SMD]"]
  R2 = Resistor [tolerance=±5% resistance=220 package="0402 [SMD]"]
  R3 = Resistor [tolerance=±5% resistance=1k package="0402 [SMD]"]
  R4 = Resistor [tolerance=±5% resistance=1k package="0402 [SMD]"]
  R5 = Resistor [tolerance=±5% resistance=2k package="0402 [SMD]"]
  R6 = Resistor [tolerance=±5% resistance=2k package="0402 [SMD]"]

nets:
  VCC: HC-SR04_Sensor_2.VCC, JACK1.POS, HC-SR04_Sensor_3.VCC, U1.VIN, LCD2004-I2C1.VCC
  N1: HC-SR04_Sensor_2.TRIG, U1.GPIO5
  N2: HC-SR04_Sensor_2.ECHO, R4.Pin_0
  GND: HC-SR04_Sensor_2.GND, JACK1.NEG, HC-SR04_Sensor_3.GND, LCD2004-I2C1.GND, LED1.cathode, LED2.cathode, R5.Pin_0
  N3: HC-SR04_Sensor_3.TRIG, U1.GPIO16
  N4: HC-SR04_Sensor_3.ECHO, R3.Pin_0
  N5: U1.GPIO25, R1.Pin_0
  N6: U1.GPIO26, R2.Pin_0
  N7: U1.GPIO17, R3.Pin_1, R5.Pin_1
  N8: U1.GPIO18, R4.Pin_1, R6.Pin_1
  N9: U1.GPIO19, J1.pulse
  N10: U1.GPIO21, LCD2004-I2C1.SDA
  N11: U1.GPIO22, LCD2004-I2C1.SCL
  N12: J1.gnd, R6.Pin_0
  N13: LED1.anode, R2.Pin_1
  N14: LED2.anode, R1.Pin_1

notes:
  DC Power Supply
  5V 3A
  mangkuk
  Tabung

custom parts:
  ESP32S-HiLetgo: HiLetgo ESP-WROOM-32 ESP32 ESP-32S Development Board 2.4GHz Dual-Mode WiFi + Bluetooth Dual Cores Microcontroller The ESP32 integrated with Antenna switches, RF Balun, power amplifiers, low-noise amplifiers, filters, and management modules, and the entire solution occupies the least area of PCB. 2.4 GHz Wi-Fi plus Bluetooth dual-mode chip, with TSMC Ultra-low power consumption 40nm technology,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
  LCD2004-I2C: A standard character display with 4x20 characters. Comes in many colors with LCM2004 IIC attached.
